// Logisim project processador.circ as structural Verilog: 3 circuits, main circuit main
module main (
  output [3:0] out_1,
  output [3:0] out_2,
  output [3:0] out_3,
  output [11:0] out_4,
  output [11:0] out_5,
  output [11:0] out_6,
  output [11:0] out_7,
  output [11:0] out_8
);

  wire clk, ctrl_imm, ctrl_w, escreve_ram, instr_pulo, le_ram, or_1_out, ula_1_lessthan, ula_1_zero;
  wire [1:0] salto;
  wire [2:0] opULA;
  wire [3:0] multiplexer_3_out, multiplexer_4_out;
  wire [11:0] adder_1_out, adder_2_out, multiplexer_1_out, multiplexer_2_out, multiplexer_5_out, PC_q,
       ram_1_dout;

  Multiplexer #(.width(12)) multiplexer_1 (
    .in0(adder_2_out), .in1(adder_1_out), .out(multiplexer_1_out), .sel(instr_pulo));
  Multiplexer #(.select(2), .width(12)) multiplexer_2 (
    .in0(adder_2_out), .in1(adder_1_out), .in2(multiplexer_1_out), .out(multiplexer_2_out), .sel(salto));  // open: in3
  ROM #(.addrWidth(4), .dataWidth(9)) rom_1 (
    .addr(out_1), .data({ctrl_w, ctrl_imm, opULA, le_ram, escreve_ram, salto}));
  // Probe on multiplexer_2_out
  Clock clock_1 (.out(clk));
  Register #(.width(12)) PC (.D(multiplexer_2_out), .en(1'b1), .clk(clk), .Q(PC_q));  // open: clr
  Adder #(.width(12)) adder_1 (.a(PC_q), .b(out_8), .out(adder_1_out));  // open: cin, cout
  Adder #(.width(12)) adder_2 (.a(PC_q), .b(12'h1), .out(adder_2_out));  // open: cin, cout
  ROM #(.addrWidth(12), .dataWidth(12)) rom_2 (.addr(PC_q), .data({out_3, out_2, out_1}));
  assign out_8 = {{8{out_2[3]}}, out_2};  // Bit_Extender bit_extender_1
  Multiplexer #(.width(4)) multiplexer_3 (.in0(out_2), .in1(4'b0000), .out(multiplexer_3_out), .sel(ctrl_imm));
  Multiplexer #(.width(4)) multiplexer_4 (
    .in0(multiplexer_3_out), .in1(out_3), .out(multiplexer_4_out), .sel(or_1_out));
  or or_1 (or_1_out, escreve_ram, le_ram);
  Multiplexer #(.width(12)) multiplexer_5 (.in0(out_4), .in1(ram_1_dout), .out(multiplexer_5_out), .sel(le_ram));
  banco_regist banco_regist_1 (
    .D(multiplexer_5_out), .w(ctrl_w), .rd(out_3), .rs1(multiplexer_4_out), .clk(clk), .rs2(out_3),
    .s1(out_5), .s2(out_6));
  Multiplexer #(.width(12)) multiplexer_6 (.in0(out_6), .in1(out_8), .out(out_7), .sel(ctrl_imm));
  RAM #(.addrWidth(12), .dataWidth(12)) ram_1 (
    .addr(out_4), .we(escreve_ram), .oe(le_ram), .clk(clk), .din(out_6), .dout(ram_1_dout));
  ULA ula_1 (.A(out_5), .B(out_7), .OPULA(opULA), .LessThan(ula_1_lessthan), .ZERO(ula_1_zero), .C(out_4));
  or or_2 (instr_pulo, ula_1_lessthan, ula_1_zero);

  // Other names for the same wires on the sheet: opcode[3:0] = out_1; endereco_ram[11:0] = out_4; imm[11:0] = out_8

  // Notes on the sheet:
  //   contents of rom_1 (hex, n*v repeats v):
  //   100 110 120 130 140 150 1b0 1b8 b4 41 41 12 2
  //   contents of rom_2 (hex, n*v repeats v):
  //   756 173 836 814 815 181 876 546 853 872 538 a77
endmodule

module banco_regist (
  input  [11:0] D,
  input  w,
  input  [3:0] rd,
  input  [3:0] rs1,
  input  clk,
  input  [3:0] rs2,
  output [11:0] s1,
  output [11:0] s2
);

  wire sd0, sd1, sd2, sd3, sd4, sd5, sd6, sd7, sd8, sd9, sd10, sd11, sd12, sd13, sd14, sd15;
  wire [11:0] multiplexer_1_out, multiplexer_2_out, multiplexer_3_out, multiplexer_4_out, multiplexer_5_out,
       multiplexer_6_out, multiplexer_7_out, multiplexer_8_out, multiplexer_9_out, multiplexer_10_out,
       multiplexer_11_out, multiplexer_12_out, multiplexer_13_out, multiplexer_14_out, multiplexer_15_out,
       vr1, vr2, vr3, vr4, vr5, vr6, vr7, vr8, vr9, vr10, vr11, vr12, vr13, vr14, vr15;

  Demultiplexer #(.select(4)) demultiplexer_1 (
    .out0(sd0), .out1(sd1), .out2(sd2), .out3(sd3), .out4(sd4), .out5(sd5), .out6(sd6), .out7(sd7),
    .out8(sd8), .out9(sd9), .out10(sd10), .out11(sd11), .out12(sd12), .out13(sd13), .out14(sd14),
    .out15(sd15), .in(w), .sel(rd));
  Register #(.width(12)) r1 (.D(multiplexer_1_out), .clk(clk), .Q(vr1));  // open: en, clr
  Multiplexer #(.width(12)) multiplexer_1 (.in0(vr1), .in1(D), .out(multiplexer_1_out), .sel(sd1));
  Register #(.width(12)) r3 (.D(multiplexer_2_out), .clk(clk), .Q(vr3));  // open: en, clr
  Multiplexer #(.width(12)) multiplexer_2 (.in0(vr3), .in1(D), .out(multiplexer_2_out), .sel(sd3));
  Register #(.width(12)) r5 (.D(multiplexer_3_out), .clk(clk), .Q(vr5));  // open: en, clr
  Multiplexer #(.width(12)) multiplexer_3 (.in0(vr5), .in1(D), .out(multiplexer_3_out), .sel(sd5));
  Register #(.width(12)) r7 (.D(multiplexer_4_out), .clk(clk), .Q(vr7));  // open: en, clr
  Multiplexer #(.width(12)) multiplexer_4 (.in0(vr7), .in1(D), .out(multiplexer_4_out), .sel(sd7));
  Multiplexer #(.width(12)) multiplexer_5 (.in0(vr8), .in1(D), .out(multiplexer_5_out), .sel(sd8));
  Multiplexer #(.width(12)) multiplexer_6 (.in0(vr10), .in1(D), .out(multiplexer_6_out), .sel(sd10));
  Multiplexer #(.width(12)) multiplexer_7 (.in0(vr12), .in1(D), .out(multiplexer_7_out), .sel(sd12));
  Multiplexer #(.width(12)) multiplexer_8 (.in0(vr14), .in1(D), .out(multiplexer_8_out), .sel(sd14));
  Register #(.width(12)) r8 (.D(multiplexer_5_out), .clk(clk), .Q(vr8));  // open: en, clr
  Register #(.width(12)) r10 (.D(multiplexer_6_out), .clk(clk), .Q(vr10));  // open: en, clr
  Register #(.width(12)) r12 (.D(multiplexer_7_out), .clk(clk), .Q(vr12));  // open: en, clr
  Register #(.width(12)) r14 (.D(multiplexer_8_out), .clk(clk), .Q(vr14));  // open: en, clr
  Register #(.width(12)) r2 (.D(multiplexer_9_out), .clk(clk), .Q(vr2));  // open: en, clr
  Multiplexer #(.width(12)) multiplexer_9 (.in0(vr2), .in1(D), .out(multiplexer_9_out), .sel(sd2));
  Register #(.width(12)) r4 (.D(multiplexer_10_out), .clk(clk), .Q(vr4));  // open: en, clr
  Multiplexer #(.width(12)) multiplexer_10 (.in0(vr4), .in1(D), .out(multiplexer_10_out), .sel(sd4));
  Register #(.width(12)) r6 (.D(multiplexer_11_out), .clk(clk), .Q(vr6));  // open: en, clr
  Multiplexer #(.width(12)) multiplexer_11 (.in0(vr6), .in1(D), .out(multiplexer_11_out), .sel(sd6));
  Multiplexer #(.width(12)) multiplexer_12 (.in0(vr9), .in1(D), .out(multiplexer_12_out), .sel(sd9));
  Multiplexer #(.width(12)) multiplexer_13 (.in0(vr11), .in1(D), .out(multiplexer_13_out), .sel(sd11));
  Multiplexer #(.width(12)) multiplexer_14 (.in0(vr13), .in1(D), .out(multiplexer_14_out), .sel(sd13));
  Multiplexer #(.width(12)) multiplexer_15 (.in0(vr15), .out(multiplexer_15_out), .sel(sd15));  // open: in1
  Register #(.width(12)) r9 (.D(multiplexer_12_out), .clk(clk), .Q(vr9));  // open: en, clr
  Register #(.width(12)) r11 (.D(multiplexer_13_out), .clk(clk), .Q(vr11));  // open: en, clr
  Register #(.width(12)) r13 (.D(multiplexer_14_out), .clk(clk), .Q(vr13));  // open: en, clr
  Register #(.width(12)) r15 (.D(multiplexer_15_out), .clk(clk), .Q(vr15));  // open: en, clr
  Multiplexer #(.select(4), .width(12)) multiplexer_16 (
    .in0({12{1'b0}}), .in1(vr1), .in2(vr2), .in3(vr3), .in4(vr4), .in5(vr5), .in6(vr6), .in7(vr7), .in8(vr8),
    .in9(vr9), .in10(vr10), .in11(vr11), .in12(vr12), .in13(vr13), .in14(vr14), .in15(vr15), .out(s1),
    .sel(rs1));
  Multiplexer #(.select(4), .width(12)) multiplexer_17 (
    .in0({12{1'b0}}), .in1(vr1), .in2(vr2), .in3(vr3), .in4(vr4), .in5(vr5), .in6(vr6), .in7(vr7), .in8(vr8),
    .in9(vr9), .in10(vr10), .in11(vr11), .in12(vr12), .in13(vr13), .in14(vr14), .in15(vr15), .out(s2),
    .sel(rs2));

  // Other names for the same wires on the sheet: vd[11:0] = D
endmodule

module ULA (
  input  [11:0] A,
  input  [11:0] B,
  input  [2:0] OPULA,
  output LessThan,
  output ZERO,
  output [11:0] C
);

  wire [11:0] adder_1_out, and_1_out, multiplier_1_out, not_1_out, or_1_out, subtractor_1_out;

  assign not_1_out = ~B;  // NOT_Gate not_1, 12 bits wide
  assign and_1_out = A & B;  // AND_Gate and_1, 12 bits wide
  assign or_1_out = A | B;  // OR_Gate or_1, 12 bits wide
  Adder #(.width(12)) adder_1 (.a(A), .b(B), .out(adder_1_out));  // open: cin, cout
  Subtractor #(.width(12)) subtractor_1 (.a(A), .b(B), .out(subtractor_1_out));  // open: bin, bout
  Multiplier #(.width(12)) multiplier_1 (.a(A), .b(B), .out(multiplier_1_out));  // open: cin, cout
  Multiplexer #(.select(3), .width(12)) multiplexer_1 (
    .in0(not_1_out), .in1(and_1_out), .in2(or_1_out), .in3(adder_1_out), .in4(subtractor_1_out),
    .in5(multiplier_1_out), .out(C), .sel(OPULA));  // open: in6, in7
  Comparator #(.width(12)) comparator_1 (.a({12{1'b0}}), .b(C), .gt(LessThan), .eq(ZERO));  // open: lt
endmodule
